// Logisim project kim_project1.circ as structural Verilog: 2 circuits, main circuit main
module main (
  input  in_1,
  input  in_2,
  input  in_3,
  input  in_4,
  input  in_5,
  input  in_6,
  input  in_7,
  input  in_8
);

  wire [3:0] hexdigital_1_out_9, hexdigital_1_out_10;

  Hex_Digit_Display hex_digit_display_1 (.value(hexdigital_1_out_9));  // open: dp
  HexDigital hexdigital_1 (
    .out_9(hexdigital_1_out_9), .out_10(hexdigital_1_out_10), .in_1(in_1), .in_2(in_2), .in_3(in_3),
    .in_4(in_4), .in_5(in_5), .in_6(in_6), .in_7(in_7), .in_8(in_8));
  Hex_Digit_Display hex_digit_display_2 (.value(hexdigital_1_out_10));  // open: dp
endmodule

module HexDigital (
  input  in_1,
  input  in_2,
  input  in_3,
  input  in_4,
  input  in_5,
  input  in_6,
  input  in_7,
  input  in_8,
  output [3:0] out_9,
  output [3:0] out_10
);


  assign out_9 = {in_1, in_2, in_3, in_4};
  assign out_10 = {in_5, in_6, in_7, in_8};
endmodule
