// Logisim project Final Project - Logisim Template.circ as structural Verilog
module main (
  input  in_1,
  input  in_2,
  input  in_3,
  input  in_4,
  input  in_5,
  input  in_6,
  input  in_7,
  input  in_8
);

  wire button_5_out;
  wire [3:0] button_out, n8_bit_calculator_1_display_3_0, n8_bit_calculator_1_display_7_4;

  Hex_Digit_Display hex_digit_display_1 (.value(n8_bit_calculator_1_display_3_0));  // open: dp
  Hex_Digit_Display hex_digit_display_2 (.value(n8_bit_calculator_1_display_7_4));  // open: dp
  _8_Bit_Calculator u_8_bit_calculator_1 (
    .Display_7_4(n8_bit_calculator_1_display_7_4), .Display_3_0(n8_bit_calculator_1_display_3_0),
    .in_3(in_1), .in_4(in_2), .in_5(in_3), .in_6(in_4), .in_7(in_5), .in_8(in_6), .in_9(in_7), .in_10(in_8),
    .Operator(button_out), .Equals(button_5_out));
  Button button (.out(button_out[0]));
  Button button_2 (.out(button_out[1]));
  Button button_3 (.out(button_out[2]));
  Button button_4 (.out(button_out[3]));
  Button button_5 (.out(button_5_out));
endmodule

module _8_Bit_Calculator (
  input  [3:0] Operator,
  input  Equals,
  input  in_3,
  input  in_4,
  input  in_5,
  input  in_6,
  input  in_7,
  input  in_8,
  input  in_9,
  input  in_10,
  output [3:0] Display_7_4,
  output [3:0] Display_3_0
);

  Datapath__FP_Part_2 Datapath (
    .Data_Out({Display_7_4, Display_3_0}), .Data_In({in_3, in_4, in_5, in_6, in_7, in_8, in_9, in_10}));
  Controller__FP_Part_1 Controller ();
endmodule

module Datapath__FP_Part_2 (
  input  [7:0] Data_In,
  output [7:0] Data_Out
);
endmodule
