// Logisim project PracticePart1.circ as structural Verilog: 1 circuit, main circuit main
module main (
  input  E,
  input  [3:0] O,
  output x,
  output y
);

  wire and_1_out, and_2_out, clock_1_out, or_1_out, or_2_out;

  and and_1 (and_1_out, ~O[0], ~O[1], ~O[2], ~O[3], E);  // AND_Gate
  or or_1 (or_1_out, O[0], O[1], O[2], O[3]);
  and and_2 (and_2_out, or_1_out, ~E);  // AND_Gate
  Clock clock_1 (.out(clock_1_out));
  Register #(.width(1)) u_x (.D(and_1_out), .en(E), .Q(x), .clk(clock_1_out), .clr(or_2_out));
  Register #(.width(1)) u_y (.D(and_2_out), .Q(y), .clk(clock_1_out), .clr(E));  // open: en
  or or_2 (or_2_out, O[0], O[1], O[2], O[3]);
endmodule
