// Logisim project kim_fp_calculator2.circ as structural Verilog: 8 circuits, main circuit 8-Bit Calculator
module main (
  input  in_1,
  input  in_2,
  input  in_3,
  input  in_4,
  input  in_5,
  input  in_6,
  input  in_7,
  input  in_8
);

  wire button_5_out;
  wire [3:0] button_out, n8_bit_calculator_1_display_3_0, n8_bit_calculator_1_display_7_4;

  Hex_Digit_Display hex_digit_display_1 (.value(n8_bit_calculator_1_display_3_0));  // open: dp
  Hex_Digit_Display hex_digit_display_2 (.value(n8_bit_calculator_1_display_7_4));  // open: dp
  _8_Bit_Calculator u_8_bit_calculator_1 (
    .Display_7_4(n8_bit_calculator_1_display_7_4), .Display_3_0(n8_bit_calculator_1_display_3_0),
    .in_3(in_1), .in_4(in_2), .in_5(in_3), .in_6(in_4), .in_7(in_5), .in_8(in_6), .in_9(in_7), .in_10(in_8),
    .Operator(button_out), .Equals(button_5_out));
  Button button (.out(button_out[0]));
  Button button_2 (.out(button_out[1]));
  Button button_3 (.out(button_out[2]));
  Button button_4 (.out(button_out[3]));
  Button button_5 (.out(button_5_out));
endmodule

module _8_Bit_Calculator (
  input  [3:0] Operator,
  input  Equals,
  input  in_3,
  input  in_4,
  input  in_5,
  input  in_6,
  input  in_7,
  input  in_8,
  input  in_9,
  input  in_10,
  output [3:0] Display_7_4,
  output [3:0] Display_3_0
);

  wire [1:0] Controller_s0;

  Controller__FP_Part_1 Controller (
    .Operator_Select(Operator), .Equals(Equals), .s1(Controller_s0[1]), .s0(Controller_s0[0]));
  Datapath__FP_Part_2 DP (
    .Data_In({in_3, in_4, in_5, in_6, in_7, in_8, in_9, in_10}), .controlBit(Controller_s0),
    .Opertor(Operator), .Equals(Equals), .Data_Out({Display_7_4, Display_3_0}));
endmodule

module Controller__FP_Part_1 (
  input  Equals,
  input  [3:0] Operator_Select,
  output s1,
  output s0
);

  wire and_1_out, and_2_out, and_3_out, and_4_out, and_5_out, and_6_out, and_7_out, and_8_out, clock_1_out,
       not_1_out, not_2_out, not_3_out, not_4_out, not_5_out, not_6_out, not_7_out, not_8_out, not_9_out,
       not_10_out, or_1_out, or_2_out, or_3_out, or_4_out;

  not not_1 (not_1_out, Operator_Select[3]);
  not not_2 (not_2_out, Operator_Select[2]);
  not not_3 (not_3_out, Operator_Select[1]);
  and and_1 (and_1_out, not_1_out, not_2_out, not_3_out, not_4_out, Equals);
  not not_4 (not_4_out, Operator_Select[0]);
  not not_5 (not_5_out, Operator_Select[0]);
  not not_6 (not_6_out, Operator_Select[1]);
  not not_7 (not_7_out, Operator_Select[2]);
  not not_8 (not_8_out, Operator_Select[3]);
  and and_2 (and_2_out, not_5_out, Operator_Select[1]);
  and and_3 (and_3_out, Operator_Select[0], not_6_out);
  and and_4 (and_4_out, not_7_out, Operator_Select[3]);
  and and_5 (and_5_out, Operator_Select[2], not_8_out);
  or or_1 (or_1_out, and_2_out, and_3_out);
  not not_9 (not_9_out, or_1_out);
  not not_10 (not_10_out, or_2_out);
  or or_2 (or_2_out, and_4_out, and_5_out);
  or or_3 (or_3_out, Operator_Select[0], Operator_Select[1], Operator_Select[2], Operator_Select[3]);
  and and_6 (and_6_out, not_9_out, or_2_out);
  or or_4 (or_4_out, and_6_out, and_7_out);
  and and_7 (and_7_out, or_1_out, not_10_out);
  and and_8 (and_8_out, or_4_out, ~Equals);  // AND_Gate
  Register #(.width(1)) register_1 (.D(and_1_out), .en(Equals), .Q(s1), .clk(clock_1_out), .clr(or_3_out));
  Clock clock_1 (.out(clock_1_out));
  Register #(.width(1)) register_2 (.D(and_8_out), .en(or_3_out), .Q(s0), .clk(clock_1_out), .clr(Equals));
endmodule

module Datapath__FP_Part_2 (
  input  [7:0] Data_In,
  input  [1:0] controlBit,
  input  Equals,
  input  [3:0] Opertor,
  output [7:0] Data_Out
);

  wire or_1_out;
  wire [7:0] alu_1_output, demultiplexer_1_out1, demultiplexer_1_out2, equals_1_o, operator_1_o;

  Demultiplexer #(.select(2), .width(8)) demultiplexer_1 (
    .out1(demultiplexer_1_out1), .out2(demultiplexer_1_out2), .in(Data_In), .sel(controlBit));  // open: out0, out3, en
  Operator operator_1 (.i(demultiplexer_1_out1), .\ø (or_1_out), .o(operator_1_o));
  Equals equals_1 (.i(demultiplexer_1_out2), .in_2(Equals), .o(equals_1_o));
  or or_1 (or_1_out, Opertor[0], Opertor[1], Opertor[2], Opertor[3]);
  ALU alu_1 (.i1(operator_1_o), .i2(equals_1_o), .\ø (Opertor), .in_3(Equals), .\output (alu_1_output));
  Multiplexer #(.select(2), .width(8)) multiplexer_1 (
    .in0({8{1'b0}}), .in1(operator_1_o), .in2(alu_1_output), .out(Data_Out), .sel(controlBit));  // open: in3, en
endmodule

// Ops
module Operator (
  input  [7:0] i,
  input  \ø ,
  output [7:0] o
);

  wire clk_out;

  Register register_1 (.D(i), .en(\ø ), .Q(o), .clk(clk_out));  // open: clr
  Clock clk (.out(clk_out));
endmodule

// EQ
module Equals (
  input  [7:0] i,
  input  in_2,
  output [7:0] o
);

  wire clk_out;

  Register register_1 (.D(i), .en(in_2), .Q(o), .clk(clk_out));  // open: clr
  Clock clk (.out(clk_out));
endmodule

module ALU (
  input  [7:0] i1,
  input  [7:0] i2,
  input  in_3,
  input  [3:0] \ø ,
  output [7:0] \output 
);

  wire clk_out;
  wire [1:0] operatorSave_output;
  wire [7:0] adder_1_out, divider_1_out, multiplexer_1_out, multiplier_1_out, subtractor_1_out;

  Adder adder_1 (.a(i1), .b(i2), .out(adder_1_out));  // open: cin, cout
  Subtractor subtractor_1 (.a(i1), .b(i2), .out(subtractor_1_out));  // open: bin, bout
  Multiplier multiplier_1 (.a(i1), .b(i2), .out(multiplier_1_out));  // open: cin, cout
  Divider divider_1 (.a(i1), .b(i2), .out(divider_1_out));  // open: upper, rem
  operatorSave operatorSave (.\ø (\ø ), .\output (operatorSave_output));
  Multiplexer #(.select(2), .width(8)) multiplexer_1 (
    .in0(divider_1_out), .in1(multiplier_1_out), .in2(subtractor_1_out), .in3(adder_1_out),
    .out(multiplexer_1_out), .sel(operatorSave_output));  // open: en
  Register register_1 (.D(multiplexer_1_out), .en(in_3), .Q(\output ), .clk(clk_out));  // open: clr
  Clock clk (.out(clk_out));

  // Notes on the sheet:
  //   1000 = Add
  //   0001 = Divide
  //   0010 = Multiply
  //   0100 = Subtract
endmodule

module operatorSave (
  input  [3:0] \ø ,
  output [1:0] \output 
);

  wire clock_1_out;
  wire [1:0] priority_encoder_1_out;

  Priority_Encoder #(.select(2)) priority_encoder_1 (
    .in0(\ø [0]), .in1(\ø [1]), .in2(\ø [2]), .in3(\ø [3]), .out(priority_encoder_1_out));  // open: gs, en_out, en_in
  Clock clock_1 (.out(clock_1_out));
  Register #(.width(2)) register_1 (.D(priority_encoder_1_out), .Q(\output ), .clk(clock_1_out));  // open: en, clr

  // Notes on the sheet:
  //   Using PRI saves the MSB
  //   0001 = Divide
  //   0010 = Multiply
  //   0100 = Subtract
  //   1000 = Add
endmodule
