// Logisim project kim_fp_part1.circ as structural Verilog: 8 circuits, main circuit 8-Bit Calculator
module main (
  input  in_1,
  input  in_2,
  input  in_3,
  input  in_4,
  input  in_5,
  input  in_6,
  input  in_7,
  input  in_8
);

  wire button_5_out;
  wire [3:0] button_out, n8_bit_calculator_1_display_3_0, n8_bit_calculator_1_display_7_4;

  Hex_Digit_Display hex_digit_display_1 (.value(n8_bit_calculator_1_display_3_0));  // open: dp
  Hex_Digit_Display hex_digit_display_2 (.value(n8_bit_calculator_1_display_7_4));  // open: dp
  _8_Bit_Calculator u_8_bit_calculator_1 (
    .Display_7_4(n8_bit_calculator_1_display_7_4), .Display_3_0(n8_bit_calculator_1_display_3_0),
    .in_3(in_1), .in_4(in_2), .in_5(in_3), .in_6(in_4), .in_7(in_5), .in_8(in_6), .in_9(in_7), .in_10(in_8),
    .Operator(button_out), .Equals(button_5_out));
  Button button (.out(button_out[0]));
  Button button_2 (.out(button_out[1]));
  Button button_3 (.out(button_out[2]));
  Button button_4 (.out(button_out[3]));
  Button button_5 (.out(button_5_out));
endmodule

module _8_Bit_Calculator (
  input  [3:0] Operator,
  input  Equals,
  input  in_3,
  input  in_4,
  input  in_5,
  input  in_6,
  input  in_7,
  input  in_8,
  input  in_9,
  input  in_10,
  output [3:0] Display_7_4,
  output [3:0] Display_3_0
);

  wire [1:0] CTRL_s0;

  Controller__FP_Part_1 CTRL (.\ø (Operator), .e(Equals), .s0(CTRL_s0[0]), .s1(CTRL_s0[1]));
  Datapath__FP_Part_2 datapath_fp_part_2_1 (
    .Data_In({in_3, in_4, in_5, in_6, in_7, in_8, in_9, in_10}), .controlBit(CTRL_s0), .\ø (Operator),
    .in_3(Equals), .Data_Out({Display_7_4, Display_3_0}));
endmodule

module Controller__FP_Part_1 (
  input  e,
  input  [3:0] \ø ,
  output s0,
  output s1
);

  wire and_1_out, and_2_out, clock_1_out, not_1_out, not_2_out, not_3_out, not_4_out, not_5_out, or_1_out,
       xor_1_out;

  not not_1 (not_1_out, \ø [0]);
  not not_2 (not_2_out, \ø [1]);
  not not_3 (not_3_out, \ø [2]);
  not not_4 (not_4_out, \ø [3]);
  ExactlyOne xor_1 (.out(xor_1_out), .in0(\ø [0]), .in1(\ø [1]), .in2(\ø [2]), .in3(\ø [3]));
  not not_5 (not_5_out, e);
  and and_1 (and_1_out, not_1_out, not_2_out, not_3_out, not_4_out, e);
  and and_2 (and_2_out, xor_1_out, not_5_out);
  or or_1 (or_1_out, \ø [0], \ø [1], \ø [2], \ø [3]);
  Register #(.width(1)) u_s0 (.D(and_1_out), .en(e), .Q(s0), .clk(clock_1_out), .clr(or_1_out));
  Clock clock_1 (.out(clock_1_out));
  Register #(.width(1)) u_s1 (.D(and_2_out), .en(or_1_out), .Q(s1), .clk(clock_1_out), .clr(e));
endmodule

// DP
module Datapath__FP_Part_2 (
  input  [7:0] Data_In,
  input  [1:0] controlBit,
  input  in_3,
  input  [3:0] \ø ,
  output [7:0] Data_Out
);

  wire or_1_out;
  wire [7:0] alu_1_output, demultiplexer_1_out1, demultiplexer_1_out2, save_eq_o, save_op_o;

  Demultiplexer #(.select(2), .width(8)) demultiplexer_1 (
    .out1(demultiplexer_1_out1), .out2(demultiplexer_1_out2), .in(Data_In), .sel(controlBit));  // open: out0, out3, en
  or or_1 (or_1_out, \ø [0], \ø [1], \ø [2], \ø [3]);
  Operator save_op (.i(demultiplexer_1_out1), .\ø (or_1_out), .o(save_op_o));
  Equals save_eq (.i(demultiplexer_1_out2), .in_2(in_3), .o(save_eq_o));
  ALU alu_1 (.i1(save_op_o), .i2(save_eq_o), .\ø (\ø ), .in_3(in_3), .\output (alu_1_output));
  Multiplexer #(.select(2), .width(8)) multiplexer_1 (
    .in0({8{1'b0}}), .in1(save_op_o), .in2(alu_1_output), .out(Data_Out), .sel(controlBit));  // open: in3, en
endmodule

module Operator (
  input  [7:0] i,
  input  \ø ,
  output [7:0] o
);

  wire clk_out;

  Register register_1 (.D(i), .en(\ø ), .Q(o), .clk(clk_out));  // open: clr
  Clock clk (.out(clk_out));
endmodule

module Equals (
  input  [7:0] i,
  input  in_2,
  output [7:0] o
);

  wire clk_out;

  Register register_1 (.D(i), .en(in_2), .Q(o), .clk(clk_out));  // open: clr
  Clock clk (.out(clk_out));
endmodule

module ALU (
  input  [7:0] i1,
  input  [7:0] i2,
  input  in_3,
  input  [3:0] \ø ,
  output [7:0] \output 
);

  wire clk_out;
  wire [1:0] operatorSave_output;
  wire [7:0] adder_1_out, divider_1_out, multiplexer_1_out, multiplier_1_out, subtractor_1_out;

  Adder adder_1 (.a(i1), .b(i2), .out(adder_1_out));  // open: cin, cout
  Subtractor subtractor_1 (.a(i1), .b(i2), .out(subtractor_1_out));  // open: bin, bout
  Multiplier multiplier_1 (.a(i1), .b(i2), .out(multiplier_1_out));  // open: cin, cout
  Divider divider_1 (.a(i1), .b(i2), .out(divider_1_out));  // open: upper, rem
  operatorSave operatorSave (.\ø (\ø ), .\output (operatorSave_output));
  Multiplexer #(.select(2), .width(8)) multiplexer_1 (
    .in0(divider_1_out), .in1(multiplier_1_out), .in2(subtractor_1_out), .in3(adder_1_out),
    .out(multiplexer_1_out), .sel(operatorSave_output));  // open: en
  Register register_1 (.D(multiplexer_1_out), .en(in_3), .Q(\output ), .clk(clk_out));  // open: clr
  Clock clk (.out(clk_out));

  // Notes on the sheet:
  //   1000 = Add
  //   0001 = Divide
  //   0010 = Multiply
  //   0100 = Subtract
endmodule

module operatorSave (
  input  [3:0] \ø ,
  output [1:0] \output 
);

  wire clock_1_out;
  wire [1:0] priority_encoder_1_out;

  Priority_Encoder #(.select(2)) priority_encoder_1 (
    .in0(\ø [0]), .in1(\ø [1]), .in2(\ø [2]), .in3(\ø [3]), .out(priority_encoder_1_out));  // open: gs, en_out, en_in
  Clock clock_1 (.out(clock_1_out));
  Register #(.width(2)) register_1 (.D(priority_encoder_1_out), .Q(\output ), .clk(clock_1_out));  // open: en, clr

  // Notes on the sheet:
  //   Using PRI saves the MSB
  //   0001 = Divide
  //   0010 = Multiply
  //   0100 = Subtract
  //   1000 = Add
endmodule
