// Logisim project FlipFlops.circ as structural Verilog: 4 circuits, main circuit main
module main (
  input  in_1,
  input  in_2,
  input  in_3,
  input  in_4,
  output out_5,
  output out_6,
  output out_7,
  output out_8,
  output out_9,
  output out_10,
  output out_11,
  output out_12,
  output out_13
);

  wire clock_1_out, clock_2_out, clock_3_out, clock_4_out;
  wire [3:0] n4_bit_d_flipflop_1_p3, n4_bit_d_flipflop_2__0_2, n4_bit_d_flipflop_3__0_2,
       n4_bit_d_flipflop_4__0_2, n4_bit_d_flipflop_5__0_2;

  Adder adder_1 ();  // open: a, b, out, cin, cout
  Clock clock_1 (.out(clock_1_out));
  Clock clock_2 (.out(clock_2_out));
  D_Latch d_latch_1 (.D(in_2), .Clk_prime(clock_2_out), .Q(out_5));  // open: Q_prime
  D_Flip_Flop d_ff_1 (.clk(clock_3_out), .D(in_3), .Q(out_10));  // open: Qn, preset, en, reset
  Clock clock_3 (.out(clock_3_out));
  // _4_Bit_D_FlipFlop 4_bit_d_flipflop_1: pin names not known; wires that end beside it: 4'b0100, clock_1_out, n4_bit_d_flipflop_1_p3
  LED led_1 (.in(out_5));
  Hex_Digit_Display hex_digit_display_1 (.value(n4_bit_d_flipflop_1_p3));  // open: dp
  LED led_2 (.in(out_6));
  D_Latch d_latch_2 (.D(out_5), .Clk_prime(clock_2_out), .Q(out_6));  // open: Q_prime
  LED led_3 (.in(out_10));
  Clock clock_4 (.out(clock_4_out));
  D_Flip_Flop d_ff_2 (.clk(clock_3_out), .D(out_10), .Q(out_11));  // open: Qn, preset, en, reset
  D_Latch d_latch_3 (.D(out_6), .Clk_prime(clock_2_out), .Q(out_7));  // open: Q_prime
  LED led_4 (.in(out_7));
  LED led_5 (.in(out_11));
  LED led_6 (.in(out_12));
  D_FlipFlop d_flipflop_1 (.D(in_4), .Clk(clock_4_out), .Q(out_12));  // open: Q_prime
  Hex_Digit_Display hex_digit_display_2 (.value(n4_bit_d_flipflop_2__0_2));  // open: dp
  _4_Bit_D_FlipFlop u_4_bit_d_flipflop_2 (
    ._0(1'b1), ._1(1'b0), ._2(1'b1), ._3(1'b0), .CLK(in_1), ._0_2(n4_bit_d_flipflop_2__0_2[0]),
    ._1_2(n4_bit_d_flipflop_2__0_2[1]), ._2_2(n4_bit_d_flipflop_2__0_2[2]), ._3_2(n4_bit_d_flipflop_2__0_2[3]));
  D_Latch d_latch_4 (.D(out_7), .Clk_prime(clock_2_out), .Q(out_8));  // open: Q_prime
  Hex_Digit_Display hex_digit_display_3 (.value(n4_bit_d_flipflop_3__0_2));  // open: dp
  _4_Bit_D_FlipFlop u_4_bit_d_flipflop_3 (
    ._0(n4_bit_d_flipflop_2__0_2[0]), ._1(n4_bit_d_flipflop_2__0_2[1]), ._2(n4_bit_d_flipflop_2__0_2[2]),
    ._3(n4_bit_d_flipflop_2__0_2[3]), .CLK(in_1), ._0_2(n4_bit_d_flipflop_3__0_2[0]),
    ._1_2(n4_bit_d_flipflop_3__0_2[1]), ._2_2(n4_bit_d_flipflop_3__0_2[2]), ._3_2(n4_bit_d_flipflop_3__0_2[3]));
  LED led_7 (.in(out_8));
  LED led_8 (.in(out_13));
  D_FlipFlop d_flipflop_2 (.D(out_12), .Clk(clock_4_out), .Q(out_13));  // open: Q_prime
  Hex_Digit_Display hex_digit_display_4 (.value(n4_bit_d_flipflop_4__0_2));  // open: dp
  _4_Bit_D_FlipFlop u_4_bit_d_flipflop_4 (
    ._0(n4_bit_d_flipflop_3__0_2[0]), ._1(n4_bit_d_flipflop_3__0_2[1]), ._2(n4_bit_d_flipflop_3__0_2[2]),
    ._3(n4_bit_d_flipflop_3__0_2[3]), .CLK(in_1), ._0_2(n4_bit_d_flipflop_4__0_2[0]),
    ._1_2(n4_bit_d_flipflop_4__0_2[1]), ._2_2(n4_bit_d_flipflop_4__0_2[2]), ._3_2(n4_bit_d_flipflop_4__0_2[3]));
  _4_Bit_D_FlipFlop u_4_bit_d_flipflop_5 (
    ._0(n4_bit_d_flipflop_4__0_2[0]), ._1(n4_bit_d_flipflop_4__0_2[1]), ._2(n4_bit_d_flipflop_4__0_2[2]),
    ._3(n4_bit_d_flipflop_4__0_2[3]), .CLK(in_1), ._0_2(n4_bit_d_flipflop_5__0_2[0]),
    ._1_2(n4_bit_d_flipflop_5__0_2[1]), ._2_2(n4_bit_d_flipflop_5__0_2[2]), ._3_2(n4_bit_d_flipflop_5__0_2[3]));
  D_Latch d_latch_5 (.D(out_8), .Clk_prime(clock_2_out), .Q(out_9));  // open: Q_prime
  Hex_Digit_Display hex_digit_display_5 (.value(n4_bit_d_flipflop_5__0_2));  // open: dp
  LED led_9 (.in(out_9));
endmodule

module D_Latch (
  input  D,
  input  Clk_prime,
  output Q_prime,
  output Q
);

  wire and_1_out, and_2_out, not_1_out;

  not not_1 (not_1_out, D);
  and and_1 (and_1_out, D, Clk_prime);
  and and_2 (and_2_out, Clk_prime, not_1_out);
  nor nor_1 (Q_prime, and_1_out, Q);
  nor nor_2 (Q, Q_prime, and_2_out);
endmodule

module D_FlipFlop (
  input  D,
  input  Clk,
  output Q_prime,
  output Q
);

  wire d_latch_1_q, not_1_out;

  D_Latch d_latch_1 (.D(D), .Clk_prime(not_1_out), .Q(d_latch_1_q));  // open: Q_prime
  not not_1 (not_1_out, Clk);
  D_Latch d_latch_2 (.D(d_latch_1_q), .Clk_prime(Clk), .Q_prime(Q_prime), .Q(Q));
endmodule

module _4_Bit_D_FlipFlop (
  input  _0,
  input  _1,
  input  _2,
  input  _3,
  input  CLK,
  output _0_2,
  output _1_2,
  output _2_2,
  output _3_2
);

  D_FlipFlop u__0 (.D(_0), .Clk(CLK), .Q(_0_2));  // open: Q_prime
  D_FlipFlop u__1 (.D(_1), .Clk(CLK), .Q(_1_2));  // open: Q_prime
  D_FlipFlop u__2 (.D(_2), .Clk(CLK), .Q(_2_2));  // open: Q_prime
  D_FlipFlop u__3 (.D(_3), .Clk(CLK), .Q(_3_2));  // open: Q_prime
endmodule
