// Logisim project kim_project2.circ as structural Verilog: 5 circuits, main circuit main
module main (
);

  wire _1_out, _3_out, _5_out, _7_out, priority_encoder_1_s0, priority_encoder_1_s1, priority_encoder_1_valid;
  wire [3:0] n4x1_mux_4_bit_1_output;

  Button _1 (.out(_1_out));
  Button _3 (.out(_3_out));
  Button _5 (.out(_5_out));
  Button _7 (.out(_7_out));
  Hex_Digit_Display hex_digit_display_1 (.value(n4x1_mux_4_bit_1_output), .dp(priority_encoder_1_valid));
  _4x1_Mux__4_Bit u_4x1_mux_4_bit_1 (
    .i0(4'b0001), .i1(4'b0011), .i2(4'b0101), .i3(4'b0111), .s1(priority_encoder_1_s1),
    .s0(priority_encoder_1_s0), .Output(n4x1_mux_4_bit_1_output));
  Priority_Encoder priority_encoder_1 (
    .i0(_1_out), .i1(_3_out), .i2(_5_out), .i3(_7_out), .s0(priority_encoder_1_s0),
    .s1(priority_encoder_1_s1), .Valid(priority_encoder_1_valid));
endmodule

module _4x1_Mux__1_Bit (
  input  i0,
  input  i1,
  input  i2,
  input  i3,
  input  s1,
  input  s0,
  output Output
);

  wire and_1_out, and_2_out, and_3_out, and_4_out, not_1_out, not_2_out;

  not not_1 (not_1_out, s1);
  not not_2 (not_2_out, s0);
  and and_1 (and_1_out, i0, not_2_out, not_1_out);
  and and_2 (and_2_out, i1, s0, not_1_out);
  and and_3 (and_3_out, i2, not_2_out, s1);
  and and_4 (and_4_out, i3, s0, s1);
  or or_1 (Output, and_1_out, and_2_out, and_3_out, and_4_out);
endmodule

module _4x1_Mux__2_Bit (
  input  i0,
  input  i1,
  input  i2,
  input  i3,
  input  i4,
  input  i5,
  input  i6,
  input  i7,
  input  s1,
  input  s0,
  output _0,
  output _1
);

  wire and_1_out, and_2_out, and_3_out, and_4_out, and_5_out, and_6_out, and_7_out, and_8_out, not_1_out,
       not_2_out;

  not not_1 (not_1_out, s1);
  not not_2 (not_2_out, s0);
  and and_1 (and_1_out, i0, not_2_out, not_1_out);
  and and_2 (and_2_out, i1, s0, not_1_out);
  and and_3 (and_3_out, i2, not_2_out, s1);
  and and_4 (and_4_out, i3, s0, s1);
  and and_5 (and_5_out, i4, not_2_out, not_1_out);
  and and_6 (and_6_out, i5, s0, not_1_out);
  and and_7 (and_7_out, i6, not_2_out, s1);
  and and_8 (and_8_out, i7, s0, s1);
  or or_1 (_0, and_1_out, and_2_out, and_3_out, and_4_out);
  or or_2 (_1, and_5_out, and_6_out, and_7_out, and_8_out);
endmodule

module _4x1_Mux__4_Bit (
  input  [3:0] i0,
  input  [3:0] i1,
  input  [3:0] i2,
  input  [3:0] i3,
  input  s1,
  input  s0,
  output [3:0] Output
);

  _4x1_Mux__1_Bit u_4x1_mux_1_bit_1 (
    .i0(i0[0]), .i1(i1[0]), .i2(i2[0]), .i3(i3[0]), .s1(s1), .s0(s0), .Output(Output[0]));
  _4x1_Mux__1_Bit u_4x1_mux_1_bit_2 (
    .i0(i0[1]), .i1(i1[1]), .i2(i2[1]), .i3(i3[1]), .s1(s1), .s0(s0), .Output(Output[1]));
  _4x1_Mux__1_Bit u_4x1_mux_1_bit_3 (
    .i0(i0[2]), .i1(i1[2]), .i2(i2[2]), .i3(i3[2]), .s1(s1), .s0(s0), .Output(Output[2]));
  _4x1_Mux__1_Bit u_4x1_mux_1_bit_4 (
    .i0(i0[3]), .i1(i1[3]), .i2(i2[3]), .i3(i3[3]), .s1(s1), .s0(s0), .Output(Output[3]));
endmodule

module Priority_Encoder (
  input  i0,
  input  i1,
  input  i2,
  input  i3,
  output s0,
  output s1,
  output Valid
);

  wire and_1_out, not_1_out;

  not not_1 (not_1_out, i2);
  and and_1 (and_1_out, i1, not_1_out);
  or or_1 (s0, and_1_out, i3);
  or or_2 (s1, i2, i3);
  or or_3 (Valid, i0, i1, i2, i3);
endmodule
